# Fritzing sketch james (saved by Fritzing 0.9.3b)
breadboards: 1

parts:
  Part1 = Arduino Nano (Rev3.0)
  Part2 = Logic Level Converter
  RESET = Momentary Switch [package=ksa_sealed_tac_switch]
  FLASH = Momentary Switch [package=ksa_sealed_tac_switch]
  IC2 = L293D [package=THT]
  U1 = ESP8266 WiFi Module [part_number=ESP8266]
  IC3 = Voltage Regulator [package=78xxl]
  LED1 = smd LED [color="Red (633nm)" package="1206 [SMD]"]
  R1 = Resistor [tolerance=±5% resistance=220 package=THT]
  M1 = DC Motor
  M2 = DC Motor
  BAT1 = Battery Holders [package=lipo-1100mAh]
  BAT2 = Battery Holders [package=lipo-1100mAh]

nets:
  N1: Part1.D1/TX, Part2.RX2_HV
  N2: Part1.D0/RX, Part2.TX2_HV
  GND: Part1.GND, Part2.GND, RESET.2, FLASH.2, IC2.0V, U1.GND, IC3.GND, R1.Pin_0, BAT2.-
  N3: Part1.D4, IC2.In_1
  N4: Part1.D5, IC2.In_2
  N5: Part1.D6, IC2.In_3
  N6: Part1.D7, IC2.In_4
  3V3: Part1.3V3, U1.VCC, U1.CH_PD
  N7: Part2.TX2_LV, U1.TXD
  N8: Part2.RX2_LV, U1.RXD
  N9: RESET.4, U1.RST
  N10: FLASH.4, U1.GPIO_0
  N11: IC2.Enable_1, IC2.+Vmotor, IC2.Enable_2, IC2.+V, IC3.OUT
  N12: IC2.Out_1_(_Controlled_by_Enable_1_), M1.pin_2
  N13: IC2.Out_2_(_Controlled_by_Enable_1_), M1.pin_1
  N14: IC2.Out_3_(_Controlled_by_Enable_2_), M2.pin_2
  N15: IC2.Out_4_(_Controlled_by_Enable_2_), M2.pin_1
  N16: U1.GPIO_2, LED1.cathode
  N17: IC3.IN, BAT1.+
  N18: LED1.anode, R1.Pin_1
  N19: BAT1.-, BAT2.+

notes:
  Note that capacitors are required for the 5V voltage regulator
  At present, the Nano needs a separate power supply

custom parts:
  ESP8266 WiFi Module: Generic WiFi Module based on the ESP8266 with onboard PCB antenna and UART communications
